// Logisim project Scrolling_display.circ as structural Verilog: 5 circuits, main circuit main
module main (
  input  Pause
);

  wire and_1_out, Clock_out, comparator_1_eq, not_1_out, not_2_out, or_1_out, Repeat_End_out,
       Reset_button_out, t_ff_1_q, zero_counter_1_output;
  wire [6:0] keyboard_1_data;
  wire [7:0] multiplexer_2_out, rom_1_data, shift_register_1_s1, shift_register_1_s2, shift_register_1_s3,
       shift_register_1_s4, shift_register_1_s5, shift_register_1_s6, shift_register_1_s7,
       shift_register_1_s8, shift_register_1_s9, shift_register_1_s10, shift_register_1_s11,
       shift_register_1_s12, shift_register_1_s13, shift_register_1_s14, shift_register_1_s15,
       shift_register_1_s16, shift_register_1_s17, shift_register_1_s18, shift_register_1_s19,
       shift_register_1_s20, shift_register_1_s21, shift_register_1_s22, shift_register_1_s23,
       shift_register_1_s24, shift_register_1_s25, shift_register_1_s26, shift_register_1_s27,
       shift_register_1_s28, shift_register_1_s29, shift_register_1_s30, shift_register_1_s31,
       shift_register_1_s32, shift_register_2_dout, shift_register_2_s1, shift_register_2_s2,
       shift_register_2_s3, shift_register_2_s4, shift_register_2_s5, shift_register_2_s6,
       shift_register_2_s7, shift_register_2_s8, shift_register_2_s9, shift_register_2_s10,
       shift_register_2_s11, shift_register_2_s12, shift_register_2_s13, shift_register_2_s14,
       shift_register_2_s15, shift_register_2_s16, shift_register_2_s17, shift_register_2_s18,
       shift_register_2_s19, shift_register_2_s20, shift_register_2_s21, shift_register_2_s22,
       shift_register_2_s23, shift_register_2_s24, shift_register_2_s25, shift_register_2_s26,
       shift_register_2_s27, shift_register_2_s28, shift_register_2_s29, shift_register_2_s30,
       shift_register_2_s31, shift_register_2_s32;
  wire [8:0] address_1__9_bit_output, bit_extender_1_out, controlled_buffer_1_out, counter_1_q,
       counter_2__9_bit_output, multiplexer_1_out, ram_1_data, register_1_q;

  and and_1 (and_1_out, ~Pause, Clock_out);  // AND_Gate
  Clock Clock (.out(Clock_out));
  Button Reset_button (.out(Reset_button_out));
  Button Repeat_End (.out(Repeat_End_out));
  Keyboard #(.buflen(64)) keyboard_1 (
    .clk(comparator_1_eq), .clr(Reset_button_out), .data(keyboard_1_data));  // open: re, avail
  assign bit_extender_1_out = {{2{1'b0}}, keyboard_1_data};  // Bit_Extender bit_extender_1
  DotMatrix #(.matrixcols(32), .matrixrows(8)) dotmatrix_1 (
    .col0(shift_register_1_s32), .col1(shift_register_1_s31), .col2(shift_register_1_s30),
    .col3(shift_register_1_s29), .col4(shift_register_1_s28), .col5(shift_register_1_s27),
    .col6(shift_register_1_s26), .col7(shift_register_1_s25), .col8(shift_register_1_s24),
    .col9(shift_register_1_s23), .col10(shift_register_1_s22), .col11(shift_register_1_s21),
    .col12(shift_register_1_s20), .col13(shift_register_1_s19), .col14(shift_register_1_s18),
    .col15(shift_register_1_s17), .col16(shift_register_1_s16), .col17(shift_register_1_s15),
    .col18(shift_register_1_s14), .col19(shift_register_1_s13), .col20(shift_register_1_s12),
    .col21(shift_register_1_s11), .col22(shift_register_1_s10), .col23(shift_register_1_s9),
    .col24(shift_register_1_s8), .col25(shift_register_1_s7), .col26(shift_register_1_s6),
    .col27(shift_register_1_s5), .col28(shift_register_1_s4), .col29(shift_register_1_s3),
    .col30(shift_register_1_s2), .col31(shift_register_1_s1));
  Address address_1 (._9_bit_Input(bit_extender_1_out), ._9_bit_Output(address_1__9_bit_output));
  Counter_part #(.width(9), .max('h1ff)) counter_1 (
    .Q(counter_1_q), .clk(and_1_out), .clr(or_1_out));  // open: load, D, count, carry
  or or_1 (or_1_out, Reset_button_out, zero_counter_1_output);
  Zero_counter zero_counter_1 (
    .RAM_output(ram_1_data), .\output (zero_counter_1_output), .Initiate_Repeat(Repeat_End_out));
  assign controlled_buffer_1_out = comparator_1_eq ? address_1__9_bit_output : 9'bz;  // Controlled_Buffer controlled_buffer_1
  Shift_Register shift_register_1 (
    .Din(shift_register_2_dout), .S1(shift_register_1_s1), .S2(shift_register_1_s2),
    .S3(shift_register_1_s3), .S4(shift_register_1_s4), .S5(shift_register_1_s5), .S6(shift_register_1_s6),
    .S7(shift_register_1_s7), .S8(shift_register_1_s8), .S9(shift_register_1_s9), .S10(shift_register_1_s10),
    .S11(shift_register_1_s11), .S12(shift_register_1_s12), .S13(shift_register_1_s13),
    .S14(shift_register_1_s14), .S15(shift_register_1_s15), .S16(shift_register_1_s16),
    .S17(shift_register_1_s17), .S18(shift_register_1_s18), .S19(shift_register_1_s19),
    .S20(shift_register_1_s20), .S21(shift_register_1_s21), .S22(shift_register_1_s22),
    .S23(shift_register_1_s23), .S24(shift_register_1_s24), .S25(shift_register_1_s25),
    .S26(shift_register_1_s26), .S27(shift_register_1_s27), .S28(shift_register_1_s28),
    .S29(shift_register_1_s29), .S30(shift_register_1_s30), .S31(shift_register_1_s31),
    .S32(shift_register_1_s32), .Enable(and_1_out), .Reset(Reset_button_out));  // open: Dout
  not not_1 (not_1_out, comparator_1_eq);
  assign controlled_buffer_1_out = not_1_out ? counter_2__9_bit_output : 9'bz;  // Controlled_Buffer controlled_buffer_2
  not not_2 (not_2_out, t_ff_1_q);
  Register #(.width(9)) register_1 (
    .D(controlled_buffer_1_out), .Q(register_1_q), .clk(and_1_out), .clr(Reset_button_out));  // open: en
  RAM #(.addrWidth(9), .dataWidth(9), .bus("separate")) ram_1 (
    .addr(counter_1_q), .din(register_1_q), .data(ram_1_data), .str(not_2_out), .clk(and_1_out),
    .clr(Reset_button_out));  // open: sel, ld
  DotMatrix #(.matrixcols(32), .matrixrows(8)) dotmatrix_2 (
    .col0(shift_register_2_s32), .col1(shift_register_2_s31), .col2(shift_register_2_s30),
    .col3(shift_register_2_s29), .col4(shift_register_2_s28), .col5(shift_register_2_s27),
    .col6(shift_register_2_s26), .col7(shift_register_2_s25), .col8(shift_register_2_s24),
    .col9(shift_register_2_s23), .col10(shift_register_2_s22), .col11(shift_register_2_s21),
    .col12(shift_register_2_s20), .col13(shift_register_2_s19), .col14(shift_register_2_s18),
    .col15(shift_register_2_s17), .col16(shift_register_2_s16), .col17(shift_register_2_s15),
    .col18(shift_register_2_s14), .col19(shift_register_2_s13), .col20(shift_register_2_s12),
    .col21(shift_register_2_s11), .col22(shift_register_2_s10), .col23(shift_register_2_s9),
    .col24(shift_register_2_s8), .col25(shift_register_2_s7), .col26(shift_register_2_s6),
    .col27(shift_register_2_s5), .col28(shift_register_2_s4), .col29(shift_register_2_s3),
    .col30(shift_register_2_s2), .col31(shift_register_2_s1));
  Counter counter_2 (._9_bit_Input(register_1_q), ._9_bit_Output(counter_2__9_bit_output));
  Multiplexer #(.width(9), .enable("false")) multiplexer_1 (
    .in0(register_1_q), .in1(ram_1_data), .out(multiplexer_1_out), .sel(t_ff_1_q));
  T_Flip_Flop t_ff_1 (.clk(Repeat_End_out), .T(1'b1), .Q(t_ff_1_q), .reset(Reset_button_out));  // open: Qn, preset, en
  Shift_Register shift_register_2 (
    .Din(multiplexer_2_out), .S1(shift_register_2_s1), .S2(shift_register_2_s2), .S3(shift_register_2_s3),
    .S4(shift_register_2_s4), .S5(shift_register_2_s5), .S6(shift_register_2_s6), .S7(shift_register_2_s7),
    .S8(shift_register_2_s8), .S9(shift_register_2_s9), .S10(shift_register_2_s10),
    .S11(shift_register_2_s11), .S12(shift_register_2_s12), .S13(shift_register_2_s13),
    .S14(shift_register_2_s14), .S15(shift_register_2_s15), .S16(shift_register_2_s16),
    .S17(shift_register_2_s17), .S18(shift_register_2_s18), .S19(shift_register_2_s19),
    .S20(shift_register_2_s20), .S21(shift_register_2_s21), .S22(shift_register_2_s22),
    .S23(shift_register_2_s23), .S24(shift_register_2_s24), .S25(shift_register_2_s25),
    .S26(shift_register_2_s26), .S27(shift_register_2_s27), .S28(shift_register_2_s28),
    .S29(shift_register_2_s29), .S30(shift_register_2_s30), .S31(shift_register_2_s31),
    .S32(shift_register_2_s32), .Dout(shift_register_2_dout), .Enable(and_1_out), .Reset(Reset_button_out));
  ROM #(.addrWidth(9)) rom_1 (.addr(multiplexer_1_out), .data(rom_1_data));  // open: sel
  Comparator comparator_1 (.a(rom_1_data), .b({8{1'b1}}), .eq(comparator_1_eq));  // open: gt, lt
  Multiplexer #(.width(8), .enable("false")) multiplexer_2 (
    .in0(rom_1_data), .in1({8{1'b0}}), .out(multiplexer_2_out), .sel(comparator_1_eq));

  // Notes on the sheet:
  //   Keyboard input
  //   Bit extender
  //   Zero counter
  //   ROM address locator
  //   Counter
  //   o/p
  //   i/p
  //   RAM Storage
  //   9 bit register
  //   LED MATRIX
  //   T Flip Flop
  //   ROM Storage
  //   contents of rom_1 (hex, n*v repeats v):
  //   ff 7e 90 90 7e ff ff ff fe 92 92 6c 4*ff fe 82 82 82 4*ff fe 82 82 7c 4*ff fe 92 92 5*ff fe 90 90
  //   5*ff fe 82 92 9e 4*ff fe 10 10 fe 4*ff 82 fe 82 5*ff c 2 2 fc 4*ff fe 38 44 82 4*ff fe 2 2 5*ff fe
  //   60 38 60 fe ff ff ff fe 60 38 c fe ff ff ff fe 82 82 fe 4*ff fe 90 f0 5*ff fe 82 8a fe 4 ff ff ff fe
  //   98 94 62 4*ff f2 92 9e 5*ff 80 fe 80 5*ff fe 2 fe 5*ff f8 6 f8 5*ff f8 6 78 6 f8 ff ff ff c6 28 10
  //   28 c6 ff ff ff f0 1e f0 5*ff 86 8a 92 a2 c2 ff ff ff fe 8a 92 a2 fe ff ff ff 22 42 fe 2 2 ff ff ff
  //   9e 92 92 92 f2 ff ff ff 82 92 92 92 fe ff ff ff f0 10 10 10 fe ff ff ff e4 a2 a2 a2 9c ff ff ff fe
  //   92 92 92 9e ff ff ff 80 8e 90 90 e0 ff ff ff fe 92 92 92 fe ff ff ff f2 92 92 92 fe ff ff ff 0 0 0
  //   5*ff fa 7*ff 80 8a 90 60 4*ff 1 2 ff 2 4*ff 8*0 18 24 42 52 34 70 ff ff 3c 42 a9 85 85 a9 42 3c ff
  //   10 0 44 aa 92 82 44 38 ff
  //   Comparator
  //   Space
endmodule

module Shift_Register (
  input  [7:0] Din,
  input  Enable,
  input  Reset,
  output [7:0] S1,
  output [7:0] S2,
  output [7:0] S3,
  output [7:0] S4,
  output [7:0] S5,
  output [7:0] S6,
  output [7:0] S7,
  output [7:0] S8,
  output [7:0] S9,
  output [7:0] S10,
  output [7:0] S11,
  output [7:0] S12,
  output [7:0] S13,
  output [7:0] S14,
  output [7:0] S15,
  output [7:0] S16,
  output [7:0] S17,
  output [7:0] S18,
  output [7:0] S19,
  output [7:0] S20,
  output [7:0] S21,
  output [7:0] S22,
  output [7:0] S23,
  output [7:0] S24,
  output [7:0] S25,
  output [7:0] S26,
  output [7:0] S27,
  output [7:0] S28,
  output [7:0] S29,
  output [7:0] S30,
  output [7:0] S31,
  output [7:0] S32,
  output [7:0] Dout
);

  Register register_1 (.D(Din), .Q(S1), .clk(Enable), .clr(Reset));  // open: en
  Register register_2 (.D(S1), .Q(S2), .clk(Enable), .clr(Reset));  // open: en
  Register register_3 (.D(S16), .Q(S17), .clk(Enable), .clr(Reset));  // open: en
  Register register_4 (.D(S17), .Q(S18), .clk(Enable), .clr(Reset));  // open: en
  Register register_5 (.D(S2), .Q(S3), .clk(Enable), .clr(Reset));  // open: en
  Register register_6 (.D(S3), .Q(S4), .clk(Enable), .clr(Reset));  // open: en
  Register register_7 (.D(S18), .Q(S19), .clk(Enable), .clr(Reset));  // open: en
  Register register_8 (.D(S19), .Q(S20), .clk(Enable), .clr(Reset));  // open: en
  Register register_9 (.D(S4), .Q(S5), .clk(Enable), .clr(Reset));  // open: en
  Register register_10 (.D(S20), .Q(S21), .clk(Enable), .clr(Reset));  // open: en
  Register register_11 (.D(S5), .Q(S6), .clk(Enable), .clr(Reset));  // open: en
  Register register_12 (.D(S6), .Q(S7), .clk(Enable), .clr(Reset));  // open: en
  Register register_13 (.D(S22), .Q(S23), .clk(Enable), .clr(Reset));  // open: en
  Register register_14 (.D(S21), .Q(S22), .clk(Enable), .clr(Reset));  // open: en
  Register register_15 (.D(S7), .Q(S8), .clk(Enable), .clr(Reset));  // open: en
  Register register_16 (.D(S23), .Q(S24), .clk(Enable), .clr(Reset));  // open: en
  Register register_17 (.D(S8), .Q(S9), .clk(Enable), .clr(Reset));  // open: en
  Register register_18 (.D(S9), .Q(S10), .clk(Enable), .clr(Reset));  // open: en
  Register register_19 (.D(S25), .Q(S26), .clk(Enable), .clr(Reset));  // open: en
  Register register_20 (.D(S24), .Q(S25), .clk(Enable), .clr(Reset));  // open: en
  Register register_21 (.D(S10), .Q(S11), .clk(Enable), .clr(Reset));  // open: en
  Register register_22 (.D(S11), .Q(S12), .clk(Enable), .clr(Reset));  // open: en
  Register register_23 (.D(S27), .Q(S28), .clk(Enable), .clr(Reset));  // open: en
  Register register_24 (.D(S26), .Q(S27), .clk(Enable), .clr(Reset));  // open: en
  Register register_25 (.D(S12), .Q(S13), .clk(Enable), .clr(Reset));  // open: en
  Register register_26 (.D(S28), .Q(S29), .clk(Enable), .clr(Reset));  // open: en
  Register register_27 (.D(S14), .Q(S15), .clk(Enable), .clr(Reset));  // open: en
  Register register_28 (.D(S13), .Q(S14), .clk(Enable), .clr(Reset));  // open: en
  Register register_29 (.D(S29), .Q(S30), .clk(Enable), .clr(Reset));  // open: en
  Register register_30 (.D(S30), .Q(S31), .clk(Enable), .clr(Reset));  // open: en
  Register register_31 (.D(S15), .Q(S16), .clk(Enable), .clr(Reset));  // open: en
  Register register_32 (.D(S31), .Q(Dout), .clk(Enable), .clr(Reset));  // open: en

  assign S32 = Dout;
endmodule

module Address (
  input  [8:0] _9_bit_Input,
  output [8:0] _9_bit_Output
);

  wire comparator_1_eq, comparator_2_eq, comparator_3_eq, comparator_4_eq, comparator_5_eq, comparator_6_eq,
       comparator_7_eq, comparator_8_eq, comparator_9_eq, comparator_10_eq, comparator_11_eq,
       comparator_12_eq, comparator_13_eq, comparator_14_eq, comparator_15_eq, comparator_16_eq,
       comparator_17_eq, comparator_18_eq, comparator_19_eq, comparator_20_eq, comparator_21_eq,
       comparator_22_eq, comparator_23_eq, comparator_24_eq, comparator_25_eq, comparator_26_eq,
       comparator_27_eq, comparator_28_eq, comparator_29_eq, comparator_30_eq, comparator_31_eq,
       comparator_32_eq, comparator_33_eq, comparator_34_eq, comparator_35_eq, comparator_36_eq,
       comparator_37_eq, comparator_38_eq, comparator_39_eq, comparator_40_eq, comparator_41_eq,
       comparator_42_eq, comparator_43_eq, comparator_44_eq, comparator_45_eq;

  Comparator #(.width(9), .mode("unsigned")) comparator_1 (
    .a(_9_bit_Input), .b(9'h61), .eq(comparator_1_eq));  // open: gt, lt
  Comparator #(.width(9), .mode("unsigned")) comparator_2 (
    .a(_9_bit_Input), .b(9'h62), .eq(comparator_2_eq));  // open: gt, lt
  Comparator #(.width(9), .mode("unsigned")) comparator_3 (
    .a(_9_bit_Input), .b(9'h63), .eq(comparator_3_eq));  // open: gt, lt
  Comparator #(.width(9), .mode("unsigned")) comparator_4 (
    .a(_9_bit_Input), .b(9'h64), .eq(comparator_4_eq));  // open: gt, lt
  Comparator #(.width(9), .mode("unsigned")) comparator_5 (
    .a(_9_bit_Input), .b(9'h65), .eq(comparator_5_eq));  // open: gt, lt
  Comparator #(.width(9), .mode("unsigned")) comparator_6 (
    .a(_9_bit_Input), .b(9'h66), .eq(comparator_6_eq));  // open: gt, lt
  Comparator #(.width(9), .mode("unsigned")) comparator_7 (
    .a(_9_bit_Input), .b(9'h67), .eq(comparator_7_eq));  // open: gt, lt
  Comparator #(.width(9), .mode("unsigned")) comparator_8 (
    .a(_9_bit_Input), .b(9'h68), .eq(comparator_8_eq));  // open: gt, lt
  Comparator #(.width(9), .mode("unsigned")) comparator_9 (
    .a(_9_bit_Input), .b(9'h69), .eq(comparator_9_eq));  // open: gt, lt
  Comparator #(.width(9), .mode("unsigned")) comparator_10 (
    .a(_9_bit_Input), .b(9'h6a), .eq(comparator_10_eq));  // open: gt, lt
  Comparator #(.width(9), .mode("unsigned")) comparator_11 (
    .a(_9_bit_Input), .b(9'h6b), .eq(comparator_11_eq));  // open: gt, lt
  Comparator #(.width(9), .mode("unsigned")) comparator_12 (
    .a(_9_bit_Input), .b(9'h6c), .eq(comparator_12_eq));  // open: gt, lt
  Comparator #(.width(9), .mode("unsigned")) comparator_13 (
    .a(_9_bit_Input), .b(9'h6d), .eq(comparator_13_eq));  // open: gt, lt
  Comparator #(.width(9), .mode("unsigned")) comparator_14 (
    .a(_9_bit_Input), .b(9'h6e), .eq(comparator_14_eq));  // open: gt, lt
  Comparator #(.width(9), .mode("unsigned")) comparator_15 (
    .a(_9_bit_Input), .b(9'h6f), .eq(comparator_15_eq));  // open: gt, lt
  assign _9_bit_Output = comparator_1_eq ? 9'h1 : 9'bz;  // Controlled_Buffer controlled_buffer_1
  assign _9_bit_Output = comparator_2_eq ? 9'h8 : 9'bz;  // Controlled_Buffer controlled_buffer_2
  assign _9_bit_Output = comparator_3_eq ? 9'h10 : 9'bz;  // Controlled_Buffer controlled_buffer_3
  assign _9_bit_Output = comparator_4_eq ? 9'h18 : 9'bz;  // Controlled_Buffer controlled_buffer_4
  assign _9_bit_Output = comparator_5_eq ? 9'h20 : 9'bz;  // Controlled_Buffer controlled_buffer_5
  assign _9_bit_Output = comparator_6_eq ? 9'h28 : 9'bz;  // Controlled_Buffer controlled_buffer_6
  assign _9_bit_Output = comparator_7_eq ? 9'h30 : 9'bz;  // Controlled_Buffer controlled_buffer_7
  assign _9_bit_Output = comparator_8_eq ? 9'h38 : 9'bz;  // Controlled_Buffer controlled_buffer_8
  assign _9_bit_Output = comparator_9_eq ? 9'h40 : 9'bz;  // Controlled_Buffer controlled_buffer_9
  assign _9_bit_Output = comparator_10_eq ? 9'h48 : 9'bz;  // Controlled_Buffer controlled_buffer_10
  assign _9_bit_Output = comparator_11_eq ? 9'h50 : 9'bz;  // Controlled_Buffer controlled_buffer_11
  assign _9_bit_Output = comparator_12_eq ? 9'h58 : 9'bz;  // Controlled_Buffer controlled_buffer_12
  assign _9_bit_Output = comparator_13_eq ? 9'h60 : 9'bz;  // Controlled_Buffer controlled_buffer_13
  assign _9_bit_Output = comparator_14_eq ? 9'h68 : 9'bz;  // Controlled_Buffer controlled_buffer_14
  assign _9_bit_Output = comparator_15_eq ? 9'h70 : 9'bz;  // Controlled_Buffer controlled_buffer_15
  Comparator #(.width(9), .mode("unsigned")) comparator_16 (
    .a(_9_bit_Input), .b(9'h70), .eq(comparator_16_eq));  // open: gt, lt
  Comparator #(.width(9), .mode("unsigned")) comparator_17 (
    .a(_9_bit_Input), .b(9'h71), .eq(comparator_17_eq));  // open: gt, lt
  Comparator #(.width(9), .mode("unsigned")) comparator_18 (
    .a(_9_bit_Input), .b(9'h72), .eq(comparator_18_eq));  // open: gt, lt
  Comparator #(.width(9), .mode("unsigned")) comparator_19 (
    .a(_9_bit_Input), .b(9'h73), .eq(comparator_19_eq));  // open: gt, lt
  Comparator #(.width(9), .mode("unsigned")) comparator_20 (
    .a(_9_bit_Input), .b(9'h74), .eq(comparator_20_eq));  // open: gt, lt
  Comparator #(.width(9), .mode("unsigned")) comparator_21 (
    .a(_9_bit_Input), .b(9'h75), .eq(comparator_21_eq));  // open: gt, lt
  Comparator #(.width(9), .mode("unsigned")) comparator_22 (
    .a(_9_bit_Input), .b(9'h76), .eq(comparator_22_eq));  // open: gt, lt
  Comparator #(.width(9), .mode("unsigned")) comparator_23 (
    .a(_9_bit_Input), .b(9'h77), .eq(comparator_23_eq));  // open: gt, lt
  Comparator #(.width(9), .mode("unsigned")) comparator_24 (
    .a(_9_bit_Input), .b(9'h78), .eq(comparator_24_eq));  // open: gt, lt
  Comparator #(.width(9), .mode("unsigned")) comparator_25 (
    .a(_9_bit_Input), .b(9'h79), .eq(comparator_25_eq));  // open: gt, lt
  Comparator #(.width(9), .mode("unsigned")) comparator_26 (
    .a(_9_bit_Input), .b(9'h7a), .eq(comparator_26_eq));  // open: gt, lt
  Comparator #(.width(9), .mode("unsigned")) comparator_27 (
    .a(_9_bit_Input), .b(9'h30), .eq(comparator_27_eq));  // open: gt, lt
  Comparator #(.width(9), .mode("unsigned")) comparator_28 (
    .a(_9_bit_Input), .b(9'h31), .eq(comparator_28_eq));  // open: gt, lt
  Comparator #(.width(9), .mode("unsigned")) comparator_29 (
    .a(_9_bit_Input), .b(9'h32), .eq(comparator_29_eq));  // open: gt, lt
  Comparator #(.width(9), .mode("unsigned")) comparator_30 (
    .a(_9_bit_Input), .b(9'h33), .eq(comparator_30_eq));  // open: gt, lt
  assign _9_bit_Output = comparator_16_eq ? 9'h78 : 9'bz;  // Controlled_Buffer controlled_buffer_16
  assign _9_bit_Output = comparator_17_eq ? 9'h80 : 9'bz;  // Controlled_Buffer controlled_buffer_17
  assign _9_bit_Output = comparator_18_eq ? 9'h88 : 9'bz;  // Controlled_Buffer controlled_buffer_18
  assign _9_bit_Output = comparator_19_eq ? 9'h90 : 9'bz;  // Controlled_Buffer controlled_buffer_19
  assign _9_bit_Output = comparator_20_eq ? 9'h98 : 9'bz;  // Controlled_Buffer controlled_buffer_20
  assign _9_bit_Output = comparator_21_eq ? 9'ha0 : 9'bz;  // Controlled_Buffer controlled_buffer_21
  assign _9_bit_Output = comparator_22_eq ? 9'ha8 : 9'bz;  // Controlled_Buffer controlled_buffer_22
  assign _9_bit_Output = comparator_23_eq ? 9'hb0 : 9'bz;  // Controlled_Buffer controlled_buffer_23
  assign _9_bit_Output = comparator_24_eq ? 9'hb8 : 9'bz;  // Controlled_Buffer controlled_buffer_24
  assign _9_bit_Output = comparator_25_eq ? 9'hc0 : 9'bz;  // Controlled_Buffer controlled_buffer_25
  assign _9_bit_Output = comparator_26_eq ? 9'hc8 : 9'bz;  // Controlled_Buffer controlled_buffer_26
  assign _9_bit_Output = comparator_27_eq ? 9'hd0 : 9'bz;  // Controlled_Buffer controlled_buffer_27
  assign _9_bit_Output = comparator_28_eq ? 9'hd8 : 9'bz;  // Controlled_Buffer controlled_buffer_28
  assign _9_bit_Output = comparator_29_eq ? 9'he0 : 9'bz;  // Controlled_Buffer controlled_buffer_29
  assign _9_bit_Output = comparator_30_eq ? 9'he8 : 9'bz;  // Controlled_Buffer controlled_buffer_30
  Comparator #(.width(9), .mode("unsigned")) comparator_31 (
    .a(_9_bit_Input), .b(9'h34), .eq(comparator_31_eq));  // open: gt, lt
  assign _9_bit_Output = comparator_31_eq ? 9'hf0 : 9'bz;  // Controlled_Buffer controlled_buffer_31
  Comparator #(.width(9), .mode("unsigned")) comparator_32 (
    .a(_9_bit_Input), .b(9'h35), .eq(comparator_32_eq));  // open: gt, lt
  assign _9_bit_Output = comparator_32_eq ? 9'hf8 : 9'bz;  // Controlled_Buffer controlled_buffer_32
  Comparator #(.width(9), .mode("unsigned")) comparator_33 (
    .a(_9_bit_Input), .b(9'h36), .eq(comparator_33_eq));  // open: gt, lt
  assign _9_bit_Output = comparator_33_eq ? 9'h100 : 9'bz;  // Controlled_Buffer controlled_buffer_33
  Comparator #(.width(9), .mode("unsigned")) comparator_34 (
    .a(_9_bit_Input), .b(9'h37), .eq(comparator_34_eq));  // open: gt, lt
  assign _9_bit_Output = comparator_34_eq ? 9'h108 : 9'bz;  // Controlled_Buffer controlled_buffer_34
  Comparator #(.width(9), .mode("unsigned")) comparator_35 (
    .a(_9_bit_Input), .b(9'h38), .eq(comparator_35_eq));  // open: gt, lt
  assign _9_bit_Output = comparator_35_eq ? 9'h110 : 9'bz;  // Controlled_Buffer controlled_buffer_35
  Comparator #(.width(9), .mode("unsigned")) comparator_36 (
    .a(_9_bit_Input), .b(9'h39), .eq(comparator_36_eq));  // open: gt, lt
  assign _9_bit_Output = comparator_36_eq ? 9'h118 : 9'bz;  // Controlled_Buffer controlled_buffer_36
  Comparator #(.width(9), .mode("unsigned")) comparator_37 (
    .a(_9_bit_Input), .b(9'h20), .eq(comparator_37_eq));  // open: gt, lt
  assign _9_bit_Output = comparator_37_eq ? 9'h120 : 9'bz;  // Controlled_Buffer controlled_buffer_37
  Comparator #(.width(9), .mode("unsigned")) comparator_38 (
    .a(_9_bit_Input), .b(9'h21), .eq(comparator_38_eq));  // open: gt, lt
  assign _9_bit_Output = comparator_38_eq ? 9'h128 : 9'bz;  // Controlled_Buffer controlled_buffer_38
  Comparator #(.width(9), .mode("unsigned")) comparator_39 (
    .a(_9_bit_Input), .b(9'h3f), .eq(comparator_39_eq));  // open: gt, lt
  assign _9_bit_Output = comparator_39_eq ? 9'h130 : 9'bz;  // Controlled_Buffer controlled_buffer_39
  Comparator #(.width(9), .mode("unsigned")) comparator_40 (
    .a(_9_bit_Input), .b(9'h2c), .eq(comparator_40_eq));  // open: gt, lt
  assign _9_bit_Output = comparator_40_eq ? 9'h138 : 9'bz;  // Controlled_Buffer controlled_buffer_40
  Comparator #(.width(9), .mode("unsigned")) comparator_41 (
    .a(_9_bit_Input), .b(9'h2e), .eq(comparator_41_eq));  // open: gt, lt
  assign _9_bit_Output = comparator_41_eq ? 9'h13b : 9'bz;  // Controlled_Buffer controlled_buffer_41
  Comparator #(.width(9), .mode("unsigned")) comparator_42 (
    .a(_9_bit_Input), .b(9'h2f), .eq(comparator_42_eq));  // open: gt, lt
  assign _9_bit_Output = comparator_42_eq ? 9'h148 : 9'bz;  // Controlled_Buffer controlled_buffer_42
  Comparator #(.width(9), .mode("unsigned")) comparator_43 (
    .a(_9_bit_Input), .b(9'h5c), .eq(comparator_43_eq));  // open: gt, lt
  assign _9_bit_Output = comparator_43_eq ? 9'h150 : 9'bz;  // Controlled_Buffer controlled_buffer_43
  Comparator #(.width(9), .mode("unsigned")) comparator_44 (
    .a(_9_bit_Input), .b(9'h2a), .eq(comparator_44_eq));  // open: gt, lt
  assign _9_bit_Output = comparator_44_eq ? 9'h159 : 9'bz;  // Controlled_Buffer controlled_buffer_44
  Comparator #(.width(9), .mode("unsigned")) comparator_45 (
    .a(_9_bit_Input), .b({9{1'b0}}), .eq(comparator_45_eq));  // open: gt, lt
  assign _9_bit_Output = comparator_45_eq ? {9{1'b0}} : 9'bz;  // Controlled_Buffer controlled_buffer_45

  // Notes on the sheet:
  //   A
  //   B
  //   C
  //   D
  //   E
  //   F
  //   G
  //   H
  //   I
  //   J
  //   K
  //   L
  //   M
  //   N
  //   O
  //   P
  //   Q
  //   R
  //   S
  //   T
  //   U
  //   V
  //   W
  //   X
  //   Y
  //   Z
  //   0
  //   1
  //   2
  //   3
  //   4
  //   5
  //   6
  //   7
  //   8
  //   9
  //   "Space"
  //   !
  //   ?
  //   ,
  //   .
  //   Arrow
  //   :)
  //   PacMan
  //   None
endmodule

module Counter (
  input  [8:0] _9_bit_Input,
  output [8:0] _9_bit_Output
);

  wire comparator_1_gt;
  wire [8:0] adder_1_out;

  Comparator #(.width(9), .mode("unsigned")) comparator_1 (
    .a(_9_bit_Input), .b({9{1'b0}}), .gt(comparator_1_gt));  // open: eq, lt
  Adder #(.width(9)) adder_1 (.a(_9_bit_Input), .b(9'h1), .out(adder_1_out));  // open: cin, cout
  Multiplexer #(.width(9)) multiplexer_1 (
    .in0({9{1'b0}}), .in1(adder_1_out), .out(_9_bit_Output), .sel(comparator_1_gt));  // open: en

  // Notes on the sheet:
  //   Comparator
  //   Adder
endmodule

module Zero_counter (
  input  Initiate_Repeat,
  input  [8:0] RAM_output,
  output \output 
);

  wire and_1_out, Clock_out, comparator_1_eq, comparator_1_gt, or_1_out, t_ff_1_q;
  wire [3:0] adder_1_out, bit_extender_1_out, register_1_q;

  T_Flip_Flop t_ff_1 (.clk(Initiate_Repeat), .T(1'b1), .Q(t_ff_1_q));  // open: Qn, preset, reset, en
  Clock Clock (.out(Clock_out));
  and and_1 (and_1_out, t_ff_1_q, Clock_out);
  Comparator #(.width(9), .mode("unsigned")) comparator_1 (
    .a(RAM_output), .b({9{1'b0}}), .gt(comparator_1_gt), .eq(comparator_1_eq));  // open: lt
  Register #(.width(4)) register_1 (.D(adder_1_out), .Q(register_1_q), .clk(and_1_out), .clr(or_1_out));  // open: en
  or or_1 (or_1_out, comparator_1_gt, \output );
  assign bit_extender_1_out = {{3{1'b0}}, comparator_1_eq};  // Bit_Extender bit_extender_1
  Adder #(.width(4)) adder_1 (.a(register_1_q), .b(bit_extender_1_out), .out(adder_1_out));  // open: cin, cout
  Comparator #(.width(4), .mode("unsigned")) comparator_2 (
    .a(register_1_q), .b(4'b1010), .eq(\output ));  // open: gt, lt

  // Notes on the sheet:
  //   Comparator
  //   Register
  //   1 to 4 bit extender
  //   Adder
  //   Comparator
endmodule
